# Fritzing sketch chef_station_simon_4btn_audio_editable (saved by Fritzing 1.0.3)

parts:
  Waveshare_ESP32-P4-POE-ETH_/_ESP32-P4-POE-ETH-NH = Waveshare ESP32-P4-POE-ETH / ESP32-P4-POE-ETH-NH
  12V_SHOW_lamp_rail = 12V_SHOW lamp rail
  5V_AUDIO_SERVO_rail = 5V_AUDIO_SERVO rail  # not connected
  COMMON_GND_rail = COMMON_GND rail
  Notes = Notes  # not connected
  Waveshare_ESP32-P4-POE-ETH_/_NH = Waveshare ESP32-P4-POE-ETH / NH  # not connected
  wp_0_0_6 = Wire waypoint
  wp_1_1_7 = Wire waypoint
  wp_2_2_8 = Wire waypoint
  R1_1k_gate = 1k Ω Resistor [Resistance=1k package=THT]
  R1_10k_gate_pulldown = 10k Ω Resistor [Resistance=10k package=THT]
  Q1_IRFB11N50APBF = Basic FET N-Channel [package="TO220 [THT]"]
  BTN1_4-terminal_plug = Camdenboss CTB0158-4 [package=THT]
  Ingredient_1_arcade_button_visual = Arcade Button (red)
  BTN1_local_GND_bus = Local GND bus
  BTN1_plug_order = BTN1 plug order  # not connected
  BTN1_resistors = BTN1 resistors  # not connected
  Q1_G_/_D_/_S = Q1 G / D / S  # not connected
  wp_4_0_18 = Wire waypoint
  wp_5_1_19 = Wire waypoint
  wp_6_2_20 = Wire waypoint
  wp_8_0_21 = Wire waypoint
  wp_9_1_22 = Wire waypoint
  wp_10_2_23 = Wire waypoint
  wp_12_0_24 = Wire waypoint
  wp_14_0_25 = Wire waypoint
  wp_16_0_26 = Wire waypoint
  wp_17_1_27 = Wire waypoint
  wp_18_2_28 = Wire waypoint
  wp_19_3_29 = Wire waypoint
  wp_20_4_30 = Wire waypoint
  wp_22_0_31 = Wire waypoint
  wp_23_1_32 = Wire waypoint
  wp_24_2_33 = Wire waypoint
  wp_26_0_34 = Wire waypoint
  wp_27_1_35 = Wire waypoint
  wp_28_2_36 = Wire waypoint
  wp_30_0_37 = Wire waypoint
  wp_31_1_38 = Wire waypoint
  wp_32_2_39 = Wire waypoint
  wp_34_0_40 = Wire waypoint
  wp_36_0_41 = Wire waypoint
  wp_38_0_42 = Wire waypoint
  wp_39_1_43 = Wire waypoint
  wp_40_2_44 = Wire waypoint
  wp_42_0_45 = Wire waypoint
  wp_43_1_46 = Wire waypoint
  wp_44_2_47 = Wire waypoint
  R2_1k_gate = 1k Ω Resistor [Resistance=1k package=THT]
  R2_10k_gate_pulldown = 10k Ω Resistor [Resistance=10k package=THT]
  Q2_IRFB11N50APBF = Basic FET N-Channel [package="TO220 [THT]"]
  BTN2_4-terminal_plug = Camdenboss CTB0158-4 [package=THT]
  Ingredient_2_arcade_button_visual = Arcade Button (green, library-art derived)
  BTN2_local_GND_bus = Local GND bus
  BTN2_plug_order = BTN2 plug order  # not connected
  BTN2_resistors = BTN2 resistors  # not connected
  Q2_G_/_D_/_S = Q2 G / D / S  # not connected
  wp_46_0_57 = Wire waypoint
  wp_47_1_58 = Wire waypoint
  wp_48_2_59 = Wire waypoint
  wp_50_0_60 = Wire waypoint
  wp_51_1_61 = Wire waypoint
  wp_52_2_62 = Wire waypoint
  wp_54_0_63 = Wire waypoint
  wp_56_0_64 = Wire waypoint
  wp_58_0_65 = Wire waypoint
  wp_59_1_66 = Wire waypoint
  wp_60_2_67 = Wire waypoint
  wp_61_3_68 = Wire waypoint
  wp_62_4_69 = Wire waypoint
  wp_64_0_70 = Wire waypoint
  wp_65_1_71 = Wire waypoint
  wp_66_2_72 = Wire waypoint
  wp_68_0_73 = Wire waypoint
  wp_69_1_74 = Wire waypoint
  wp_70_2_75 = Wire waypoint
  wp_72_0_76 = Wire waypoint
  wp_73_1_77 = Wire waypoint
  wp_74_2_78 = Wire waypoint
  wp_76_0_79 = Wire waypoint
  wp_78_0_80 = Wire waypoint
  wp_80_0_81 = Wire waypoint
  wp_81_1_82 = Wire waypoint
  wp_82_2_83 = Wire waypoint
  wp_84_0_84 = Wire waypoint
  wp_85_1_85 = Wire waypoint
  wp_86_2_86 = Wire waypoint
  R3_1k_gate = 1k Ω Resistor [Resistance=1k package=THT]
  R3_10k_gate_pulldown = 10k Ω Resistor [Resistance=10k package=THT]
  Q3_IRFB11N50APBF = Basic FET N-Channel [package="TO220 [THT]"]
  BTN3_4-terminal_plug = Camdenboss CTB0158-4 [package=THT]
  Ingredient_3_arcade_button_visual = Arcade Button (white)
  BTN3_local_GND_bus = Local GND bus
  BTN3_plug_order = BTN3 plug order  # not connected
  BTN3_resistors = BTN3 resistors  # not connected
  Q3_G_/_D_/_S = Q3 G / D / S  # not connected
  wp_88_0_96 = Wire waypoint
  wp_89_1_97 = Wire waypoint
  wp_90_2_98 = Wire waypoint
  wp_92_0_99 = Wire waypoint
  wp_93_1_100 = Wire waypoint
  wp_94_2_101 = Wire waypoint
  wp_96_0_102 = Wire waypoint
  wp_98_0_103 = Wire waypoint
  wp_100_0_104 = Wire waypoint
  wp_101_1_105 = Wire waypoint
  wp_102_2_106 = Wire waypoint
  wp_103_3_107 = Wire waypoint
  wp_104_4_108 = Wire waypoint
  wp_106_0_109 = Wire waypoint
  wp_107_1_110 = Wire waypoint
  wp_108_2_111 = Wire waypoint
  wp_110_0_112 = Wire waypoint
  wp_111_1_113 = Wire waypoint
  wp_112_2_114 = Wire waypoint
  wp_114_0_115 = Wire waypoint
  wp_115_1_116 = Wire waypoint
  wp_116_2_117 = Wire waypoint
  wp_118_0_118 = Wire waypoint
  wp_120_0_119 = Wire waypoint
  wp_122_0_120 = Wire waypoint
  wp_123_1_121 = Wire waypoint
  wp_124_2_122 = Wire waypoint
  wp_126_0_123 = Wire waypoint
  wp_127_1_124 = Wire waypoint
  wp_128_2_125 = Wire waypoint
  R4_1k_gate = 1k Ω Resistor [Resistance=1k package=THT]
  R4_10k_gate_pulldown = 10k Ω Resistor [Resistance=10k package=THT]
  Q4_IRFB11N50APBF = Basic FET N-Channel [package="TO220 [THT]"]
  BTN4_4-terminal_plug = Camdenboss CTB0158-4 [package=THT]
  Ingredient_4_arcade_button_visual = Arcade Button (yellow)
  BTN4_local_GND_bus = Local GND bus
  BTN4_plug_order = BTN4 plug order  # not connected
  BTN4_resistors = BTN4 resistors  # not connected
  Q4_G_/_D_/_S = Q4 G / D / S  # not connected
  wp_130_0_135 = Wire waypoint
  wp_131_1_136 = Wire waypoint
  wp_132_2_137 = Wire waypoint
  wp_134_0_138 = Wire waypoint
  wp_135_1_139 = Wire waypoint
  wp_136_2_140 = Wire waypoint
  wp_138_0_141 = Wire waypoint
  wp_140_0_142 = Wire waypoint
  wp_142_0_143 = Wire waypoint
  wp_143_1_144 = Wire waypoint
  wp_144_2_145 = Wire waypoint
  wp_145_3_146 = Wire waypoint
  wp_146_4_147 = Wire waypoint
  wp_148_0_148 = Wire waypoint
  wp_149_1_149 = Wire waypoint
  wp_150_2_150 = Wire waypoint
  wp_152_0_151 = Wire waypoint
  wp_153_1_152 = Wire waypoint
  wp_154_2_153 = Wire waypoint
  wp_156_0_154 = Wire waypoint
  wp_157_1_155 = Wire waypoint
  wp_158_2_156 = Wire waypoint
  wp_160_0_157 = Wire waypoint
  wp_162_0_158 = Wire waypoint
  wp_164_0_159 = Wire waypoint
  wp_165_1_160 = Wire waypoint
  wp_166_2_161 = Wire waypoint
  wp_168_0_162 = Wire waypoint
  wp_169_1_163 = Wire waypoint
  wp_170_2_164 = Wire waypoint
  Optional_Simon_audio = Optional Simon audio  # not connected

nets:
  N1: Waveshare_ESP32-P4-POE-ETH_/_ESP32-P4-POE-ETH-NH.GND, COMMON_GND_rail.tap_0, COMMON_GND_rail.tap_16, COMMON_GND_rail.tap_17, COMMON_GND_rail.tap_18, COMMON_GND_rail.tap_19, wp_0_0_6.waypoint, wp_1_1_7.waypoint, wp_2_2_8.waypoint, R1_10k_gate_pulldown.Pin_1, Q1_IRFB11N50APBF.source, BTN1_4-terminal_plug.pin4, Ingredient_1_arcade_button_visual.no_name_yet#2, BTN1_local_GND_bus.ground_tap_0, BTN1_local_GND_bus.ground_tap_1, BTN1_local_GND_bus.ground_tap_4, BTN1_local_GND_bus.ground_tap_5, wp_12_0_24.waypoint, wp_14_0_25.waypoint, wp_34_0_40.waypoint, wp_36_0_41.waypoint, wp_42_0_45.waypoint, wp_43_1_46.waypoint, wp_44_2_47.waypoint, R2_10k_gate_pulldown.Pin_1, Q2_IRFB11N50APBF.source, BTN2_4-terminal_plug.pin4, Ingredient_2_arcade_button_visual.no_name_yet#2, BTN2_local_GND_bus.ground_tap_0, BTN2_local_GND_bus.ground_tap_1, BTN2_local_GND_bus.ground_tap_4, BTN2_local_GND_bus.ground_tap_5, wp_54_0_63.waypoint, wp_56_0_64.waypoint, wp_76_0_79.waypoint, wp_78_0_80.waypoint, wp_84_0_84.waypoint, wp_85_1_85.waypoint, wp_86_2_86.waypoint, R3_10k_gate_pulldown.Pin_1, Q3_IRFB11N50APBF.source, BTN3_4-terminal_plug.pin4, Ingredient_3_arcade_button_visual.no_name_yet#2, BTN3_local_GND_bus.ground_tap_0, BTN3_local_GND_bus.ground_tap_1, BTN3_local_GND_bus.ground_tap_4, BTN3_local_GND_bus.ground_tap_5, wp_96_0_102.waypoint, wp_98_0_103.waypoint, wp_118_0_118.waypoint, wp_120_0_119.waypoint, wp_126_0_123.waypoint, wp_127_1_124.waypoint, wp_128_2_125.waypoint, R4_10k_gate_pulldown.Pin_1, Q4_IRFB11N50APBF.source, BTN4_4-terminal_plug.pin4, Ingredient_4_arcade_button_visual.no_name_yet#2, BTN4_local_GND_bus.ground_tap_0, BTN4_local_GND_bus.ground_tap_1, BTN4_local_GND_bus.ground_tap_4, BTN4_local_GND_bus.ground_tap_5, wp_138_0_141.waypoint, wp_140_0_142.waypoint, wp_160_0_157.waypoint, wp_162_0_158.waypoint, wp_168_0_162.waypoint, wp_169_1_163.waypoint, wp_170_2_164.waypoint
  N2: Waveshare_ESP32-P4-POE-ETH_/_ESP32-P4-POE-ETH-NH.GPIO16, BTN1_4-terminal_plug.pin3, Ingredient_1_arcade_button_visual.no_name_yet#1, wp_16_0_26.waypoint, wp_17_1_27.waypoint, wp_18_2_28.waypoint, wp_19_3_29.waypoint, wp_20_4_30.waypoint, wp_38_0_42.waypoint, wp_39_1_43.waypoint, wp_40_2_44.waypoint
  N3: Waveshare_ESP32-P4-POE-ETH_/_ESP32-P4-POE-ETH-NH.GPIO17, BTN2_4-terminal_plug.pin3, Ingredient_2_arcade_button_visual.no_name_yet#1, wp_58_0_65.waypoint, wp_59_1_66.waypoint, wp_60_2_67.waypoint, wp_61_3_68.waypoint, wp_62_4_69.waypoint, wp_80_0_81.waypoint, wp_81_1_82.waypoint, wp_82_2_83.waypoint
  N4: Waveshare_ESP32-P4-POE-ETH_/_ESP32-P4-POE-ETH-NH.GPIO18, BTN3_4-terminal_plug.pin3, Ingredient_3_arcade_button_visual.no_name_yet#1, wp_100_0_104.waypoint, wp_101_1_105.waypoint, wp_102_2_106.waypoint, wp_103_3_107.waypoint, wp_104_4_108.waypoint, wp_122_0_120.waypoint, wp_123_1_121.waypoint, wp_124_2_122.waypoint
  N5: Waveshare_ESP32-P4-POE-ETH_/_ESP32-P4-POE-ETH-NH.GPIO19, BTN4_4-terminal_plug.pin3, Ingredient_4_arcade_button_visual.no_name_yet#1, wp_142_0_143.waypoint, wp_143_1_144.waypoint, wp_144_2_145.waypoint, wp_145_3_146.waypoint, wp_146_4_147.waypoint, wp_164_0_159.waypoint, wp_165_1_160.waypoint, wp_166_2_161.waypoint
  N6: Waveshare_ESP32-P4-POE-ETH_/_ESP32-P4-POE-ETH-NH.GPIO20, R1_1k_gate.Pin_0, wp_22_0_31.waypoint, wp_23_1_32.waypoint, wp_24_2_33.waypoint
  N7: Waveshare_ESP32-P4-POE-ETH_/_ESP32-P4-POE-ETH-NH.GPIO21, R2_1k_gate.Pin_0, wp_64_0_70.waypoint, wp_65_1_71.waypoint, wp_66_2_72.waypoint
  N8: Waveshare_ESP32-P4-POE-ETH_/_ESP32-P4-POE-ETH-NH.GPIO22, R3_1k_gate.Pin_0, wp_106_0_109.waypoint, wp_107_1_110.waypoint, wp_108_2_111.waypoint
  N9: Waveshare_ESP32-P4-POE-ETH_/_ESP32-P4-POE-ETH-NH.GPIO23, R4_1k_gate.Pin_0, wp_148_0_148.waypoint, wp_149_1_149.waypoint, wp_150_2_150.waypoint
  N10: 12V_SHOW_lamp_rail.tap_1, 12V_SHOW_lamp_rail.tap_2, 12V_SHOW_lamp_rail.tap_3, 12V_SHOW_lamp_rail.tap_4, BTN1_4-terminal_plug.pin1, wp_4_0_18.waypoint, wp_5_1_19.waypoint, wp_6_2_20.waypoint, BTN2_4-terminal_plug.pin1, wp_46_0_57.waypoint, wp_47_1_58.waypoint, wp_48_2_59.waypoint, BTN3_4-terminal_plug.pin1, wp_88_0_96.waypoint, wp_89_1_97.waypoint, wp_90_2_98.waypoint, BTN4_4-terminal_plug.pin1, wp_130_0_135.waypoint, wp_131_1_136.waypoint, wp_132_2_137.waypoint
  N11: R1_1k_gate.Pin_1, R1_10k_gate_pulldown.Pin_0, Q1_IRFB11N50APBF.gate, wp_26_0_34.waypoint, wp_27_1_35.waypoint, wp_28_2_36.waypoint, wp_30_0_37.waypoint, wp_31_1_38.waypoint, wp_32_2_39.waypoint
  N12: Q1_IRFB11N50APBF.drain, BTN1_4-terminal_plug.pin2, wp_8_0_21.waypoint, wp_9_1_22.waypoint, wp_10_2_23.waypoint
  N13: R2_1k_gate.Pin_1, R2_10k_gate_pulldown.Pin_0, Q2_IRFB11N50APBF.gate, wp_68_0_73.waypoint, wp_69_1_74.waypoint, wp_70_2_75.waypoint, wp_72_0_76.waypoint, wp_73_1_77.waypoint, wp_74_2_78.waypoint
  N14: Q2_IRFB11N50APBF.drain, BTN2_4-terminal_plug.pin2, wp_50_0_60.waypoint, wp_51_1_61.waypoint, wp_52_2_62.waypoint
  N15: R3_1k_gate.Pin_1, R3_10k_gate_pulldown.Pin_0, Q3_IRFB11N50APBF.gate, wp_110_0_112.waypoint, wp_111_1_113.waypoint, wp_112_2_114.waypoint, wp_114_0_115.waypoint, wp_115_1_116.waypoint, wp_116_2_117.waypoint
  N16: Q3_IRFB11N50APBF.drain, BTN3_4-terminal_plug.pin2, wp_92_0_99.waypoint, wp_93_1_100.waypoint, wp_94_2_101.waypoint
  N17: R4_1k_gate.Pin_1, R4_10k_gate_pulldown.Pin_0, Q4_IRFB11N50APBF.gate, wp_152_0_151.waypoint, wp_153_1_152.waypoint, wp_154_2_153.waypoint, wp_156_0_154.waypoint, wp_157_1_155.waypoint, wp_158_2_156.waypoint
  N18: Q4_IRFB11N50APBF.drain, BTN4_4-terminal_plug.pin2, wp_134_0_138.waypoint, wp_135_1_139.waypoint, wp_136_2_140.waypoint

custom parts:
  Arcade Button (green, library-art derived): Adafruit Arcade Button (green, library-art derived)
